# Fritzing sketch Mouse_City_Circuit (saved by Fritzing 0.9.9b)
breadboards: 1
perfboards: 1
stripboards: 1

parts:
  Part1 = Audio FX Sound Board + 2x2W Amp
  WeMos_D1_Mini1 = WeMos D1 Mini  # not connected
  R1 = Resistor [tolerance=±5% resistance=470 package="1206 [SMD]"]  # not connected
  JP1 = Header 1 [package=1x01_offset]  # not connected
  C1 = Electrolytic Capacitor [capacitance=1000µF voltage=35V package="300 mil [THT, electrolytic]"]
  J1 = Screw terminal - 2 pins [package=THT]  # not connected
  JP7 = Header 1 [package=1x01_offset]  # not connected
  JP8 = Header 1 [package=1x01_offset]  # not connected
  JP9 = Header 1 [package=1x01_offset]  # not connected
  JP10 = Header 1 [package=1x01_offset]  # not connected
  JP11 = Header 1 [package=1x01_offset]  # not connected
  JP12 = Header 1 [package=1x01_offset]  # not connected

nets:
  N1: Part1.GND, C1.-

custom parts:
  Audio FX Sound Board + 2x2W Amp: The Adafruit Sound Board, the fastest way to add audio effects to a project!
